# Fritzing sketch mb-app-thermostatFan-circuit (saved by Fritzing 0.9.3b)
breadboards: 1

parts:
  R1 = BBC MicroBit
  F1 = Fan - Ventilador [package=THT]
  S1 = Pushbutton [package="[THT]"]
  S2 = Pushbutton [package="[SMD]"]
  J1 = Screw terminal - 2 pins [package=THT]
  Q1 = NPN-Transistor [package="TO92 [THT]"]
  R2 = Resistor [tolerance=±5% resistance=2.2k package=THT]
  S3 = Pushbutton [package="[SMD]"]

nets:
  N1: R1.GND, S1.Pin_1, S1.Pin_2, S2.Pin_1, S2.Pin_2, Q1.E, S3.Pin_1, S3.Pin_2
  3V3: R1.3v3, F1.5V, J1.pin1
  N2: R1.P2_-_ANALOG_IN, S3.Pin_3, S3.Pin_4
  N3: R1.P11_BUTTON_B, S2.Pin_3, S2.Pin_4
  N4: R1.P5_BUTTON_A, S1.Pin_3, S1.Pin_4
  N5: R1.P0_ANALOG_IN, R2.Pin_0
  N6: F1.GND, J1.pin2, Q1.C
  N7: Q1.B, R2.Pin_1

notes:
  There isn't a fritz file of the breakout board, so I've shown the connections that go direct to the Micro:bit

custom parts:
  BBC MicroBit: The BBC MICRO:BIT
  Fan - Ventilador: Ventilador de 2 pines, se encuentra comunmente en computadoras de escritorio
